// Logisim project main.circ as structural Verilog: 1 circuit, main circuit main
module main (
  input  in_1,
  input  in_2,
  input  in_3,
  input  in_4,
  input  in_5,
  input  in_6,
  input  in_7,
  input  in_8,
  input  in_9,
  input  in_10,
  input  in_11,
  input  in_12,
  output out_13,
  output out_14,
  output out_15,
  output out_16
);

  // _74381 74381_1: pin names not known; wires that end beside it: 1'b1, in_6, in_7, in_10, in_11, in_5, in_8, in_9, in_12, in_4, in_1, in_3, in_2, out_13, out_16, out_14, out_15, 1'b0
endmodule
